// Logisim project ALU.circ as structural Verilog
module ALU (
  input  [31:0] A,
  input  [31:0] B,
  input  [4:0] Shift,
  input  [3:0] Codop,
  input  CarryIn,
  output [31:0] S,
  output [3:0] Flags
);

  wire adder_1_cout, adder_2_cout, and_4_out, and_5_out, and_6_out, bitselector_1_out, bitselector_2_out,
       bitselector_3_out, bitselector_4_out, bitselector_5_out, bitselector_6_out, bitselector_7_out,
       bitselector_8_out, bitselector_9_out, bitselector_10_out, subtractor_1_bout, subtractor_2_bout,
       subtractor_3_bout, xnor_1_out, xnor_2_out, xnor_4_out;
  wire [31:0] adder_1_out, adder_2_out, and_1_out, and_3_out, multiplier_1_cout, multiplier_1_out, not_1_out,
       or_1_out, shifter_1_out, shifter_2_out, shifter_3_out, shifter_4_out, subtractor_1_out,
       subtractor_2_out, subtractor_3_out, xor_1_out;

  BitSelector #(.width(32)) bitselector_1 (.in(A), .out(bitselector_1_out), .sel({5{1'b1}}));
  BitSelector #(.width(32)) bitselector_2 (.in(B), .out(bitselector_2_out), .sel({5{1'b1}}));
  BitSelector #(.width(32)) bitselector_3 (.in(B), .out(bitselector_3_out), .sel({5{1'b1}}));
  BitSelector #(.width(32)) bitselector_4 (.in(A), .out(bitselector_4_out), .sel({5{1'b1}}));
  assign not_1_out = ~B;  // NOT_Gate not_1, 32 bits wide
  xnor xnor_1 (xnor_1_out, bitselector_1_out, bitselector_2_out);
  xnor xnor_2 (xnor_2_out, ~bitselector_3_out, bitselector_4_out);  // XNOR_Gate
  assign and_1_out = A & B;  // AND_Gate and_1, 32 bits wide
  assign xor_1_out = A ^ B;  // XOR_Gate xor_1, 32 bits wide
  Shifter #(.width(32)) shifter_1 (.in(B), .\dist (Shift), .out(shifter_1_out));
  Shifter #(.shift("lr"), .width(32)) shifter_2 (.in(B), .\dist (Shift), .out(shifter_2_out));
  Shifter #(.shift("ar"), .width(32)) shifter_3 (.in(B), .\dist (Shift), .out(shifter_3_out));
  Adder #(.width(32)) adder_1 (.a(A), .b(B), .out(adder_1_out), .cin(CarryIn), .cout(adder_1_cout));
  Subtractor #(.width(32)) subtractor_1 (.a(A), .b(B), .out(subtractor_1_out), .bin(CarryIn), .bout(subtractor_1_bout));
  Shifter #(.shift("rr"), .width(32)) shifter_4 (.in(B), .\dist (Shift), .out(shifter_4_out));
  // AND_Gate and_2 has open pins: in0=A, in1=B, out=open
  Subtractor #(.width(32)) subtractor_2 (
    .a({32{1'b0}}), .b(A), .out(subtractor_2_out), .bout(subtractor_2_bout));  // open: bin
  Subtractor #(.width(32)) subtractor_3 (.a(B), .b(A), .out(subtractor_3_out), .bin(CarryIn), .bout(subtractor_3_bout));
  Adder #(.width(32)) adder_2 (.a(A), .b(B), .out(adder_2_out), .cin(CarryIn), .cout(adder_2_cout));
  assign or_1_out = A | B;  // OR_Gate or_1, 32 bits wide
  Multiplier #(.width(32)) multiplier_1 (.a(A), .b(B), .out(multiplier_1_out), .cout(multiplier_1_cout));  // open: cin
  assign and_3_out = A & ~B;  // AND_Gate and_3, 32 bits wide
  BitSelector #(.width(32)) bitselector_5 (.in(adder_1_out), .out(bitselector_5_out), .sel({5{1'b1}}));
  BitSelector #(.width(32)) bitselector_6 (.in(subtractor_3_out), .out(bitselector_6_out), .sel({5{1'b1}}));
  BitSelector #(.width(32)) bitselector_7 (.in(A), .out(bitselector_7_out), .sel({5{1'b1}}));
  // XNOR_Gate xnor_3 has open pins: in0=bitselector_5_out, out=open
  xnor xnor_4 (xnor_4_out, bitselector_6_out, bitselector_7_out);
  buf and_4 (and_4_out, xnor_1_out);  // AND_Gate AND_Gate
  BitSelector #(.width(32)) bitselector_8 (.in(shifter_4_out), .out(bitselector_8_out), .sel({5{1'b1}}));
  BitSelector #(.width(32)) bitselector_9 (.in(adder_2_out), .out(bitselector_9_out), .sel({5{1'b1}}));
  Multiplexer #(.enable("false"), .select(4), .width(32)) multiplexer_1 (
    .in0(and_1_out), .in1(xor_1_out), .in2(shifter_1_out), .in3(shifter_2_out), .in4(shifter_3_out),
    .in5(adder_1_out), .in6(subtractor_1_out), .in7(shifter_4_out), .in9(subtractor_2_out),
    .in10(subtractor_3_out), .in11(adder_2_out), .in12(or_1_out), .in13(multiplier_1_out), .in14(and_3_out),
    .in15(not_1_out), .out(S), .sel(Codop));  // open: in8
  BitSelector #(.width(32)) bitselector_10 (.in(multiplier_1_cout), .out(bitselector_10_out), .sel({5{1'b0}}));
  and and_5 (and_5_out, xnor_1_out, ~bitselector_9_out);  // AND_Gate
  and and_6 (and_6_out, xnor_4_out, xnor_2_out);
  BitSelector #(.width(32)) bitselector_11 (.in(S), .out(Flags[0]), .sel({5{1'b1}}));
  Comparator #(.width(32)) comparator_1 (.a(S), .b({32{1'b0}}), .eq(Flags[1]));  // open: gt, lt
  Multiplexer #(.enable("false"), .select(4)) multiplexer_2 (
    .in5(adder_1_cout), .in6(subtractor_1_bout), .in7(bitselector_8_out), .in10(subtractor_2_bout),
    .in11(subtractor_3_bout), .in12(adder_2_cout), .in13(bitselector_10_out), .out(Flags[2]), .sel(Codop));  // open: in0, in1, in2, in3, in4, in8, in9, in14, in15
  Multiplexer #(.enable("false"), .select(4)) multiplexer_3 (
    .in5(and_4_out), .in10(and_6_out), .in11(and_5_out), .out(Flags[3]), .sel(Codop));  // open: in0, in1, in2, in3, in4, in6, in7, in8, in9, in12, in13, in14, in15

  // Notes on the sheet:
  //   Note: for ROR, C = N
  //   Note 2: assume that shift > 0 for LSL and LSR
endmodule
