// Logisim project ALU.circ as structural Verilog
module ALU (
  input  [31:0] A,
  input  [31:0] B,
  input  [4:0] Shift,
  input  [3:0] Codop,
  input  CarryIn,
  output [31:0] S,
  output [3:0] Flags
);

  wire adder_1_cout, adder_2_cout, and_4_out, and_5_out, and_6_out, and_7_out, bitselector_1_out,
       bitselector_2_out, bitselector_3_out, bitselector_4_out, bitselector_5_out, bitselector_6_out,
       bitselector_7_out, bitselector_8_out, bitselector_9_out, bitselector_10_out, bitselector_11_out,
       bitselector_12_out, bitselector_13_out, not_1_out, subtractor_1_bout, subtractor_3_bout, xnor_1_out,
       xnor_2_out, xnor_3_out, xnor_4_out, xor_2_out, xor_3_out;
  wire [4:0] subtractor_4_out, subtractor_5_out;
  wire [31:0] adder_1_out, adder_2_out, and_1_out, and_2_out, and_3_out, multiplexer_1_out,
       multiplier_1_cout, multiplier_1_out, not_2_out, or_1_out, shifter_1_out, shifter_2_out, shifter_3_out,
       shifter_4_out, subtractor_1_out, subtractor_2_out, subtractor_3_out, xor_1_out;

  BitSelector #(.width(32)) bitselector_1 (.in(A), .out(bitselector_1_out), .sel({5{1'b1}}));
  BitSelector #(.width(32)) bitselector_2 (.in(B), .out(bitselector_2_out), .sel({5{1'b1}}));
  BitSelector #(.width(32)) bitselector_3 (.in(B), .out(bitselector_3_out), .sel({5{1'b1}}));
  BitSelector #(.width(32)) bitselector_4 (.in(A), .out(bitselector_4_out), .sel({5{1'b1}}));
  xnor xnor_1 (xnor_1_out, bitselector_1_out, bitselector_2_out);
  xnor xnor_2 (xnor_2_out, ~bitselector_3_out, bitselector_4_out);  // XNOR_Gate
  assign and_1_out = A & B;  // AND_Gate and_1, 32 bits wide
  assign xor_1_out = A ^ B;  // XOR_Gate xor_1, 32 bits wide
  Shifter #(.width(32)) shifter_1 (.in(B), .\dist (Shift), .out(shifter_1_out));
  Shifter #(.shift("lr"), .width(32)) shifter_2 (.in(B), .\dist (Shift), .out(shifter_2_out));
  Shifter #(.shift("ar"), .width(32)) shifter_3 (.in(B), .\dist (Shift), .out(shifter_3_out));
  Adder #(.width(32)) adder_1 (.a(A), .b(B), .out(adder_1_out), .cin(CarryIn), .cout(adder_1_cout));
  not not_1 (not_1_out, CarryIn);
  Subtractor #(.width(32)) subtractor_1 (
    .a(B), .b(A), .out(subtractor_1_out), .bin(not_1_out), .bout(subtractor_1_bout));
  Shifter #(.shift("rr"), .width(32)) shifter_4 (.in(B), .\dist (Shift), .out(shifter_4_out));
  assign and_2_out = A & B;  // AND_Gate and_2, 32 bits wide
  Subtractor #(.width(32)) subtractor_2 (.a({32{1'b0}}), .b(A), .out(subtractor_2_out));  // open: bin, bout
  Subtractor #(.width(32)) subtractor_3 (.a(B), .b(A), .out(subtractor_3_out), .bin(CarryIn), .bout(subtractor_3_bout));
  Adder #(.width(32)) adder_2 (.a(A), .b(B), .out(adder_2_out), .cin(CarryIn), .cout(adder_2_cout));
  assign or_1_out = A | B;  // OR_Gate or_1, 32 bits wide
  Multiplier #(.width(32)) multiplier_1 (.a(A), .b(B), .out(multiplier_1_out), .cout(multiplier_1_cout));  // open: cin
  assign and_3_out = ~A & B;  // AND_Gate and_3, 32 bits wide
  assign not_2_out = ~B;  // NOT_Gate not_2, 32 bits wide
  BitSelector #(.width(32)) bitselector_5 (.in(adder_1_out), .out(bitselector_5_out), .sel({5{1'b1}}));
  BitSelector #(.width(32)) bitselector_6 (.in(adder_2_out), .out(bitselector_6_out), .sel({5{1'b1}}));
  BitSelector #(.width(32)) bitselector_7 (.in(subtractor_3_out), .out(bitselector_7_out), .sel({5{1'b1}}));
  BitSelector #(.width(32)) bitselector_8 (.in(A), .out(bitselector_8_out), .sel({5{1'b1}}));
  BitSelector #(.width(32)) bitselector_9 (.in(subtractor_3_out), .out(bitselector_9_out), .sel({5{1'b1}}));
  BitSelector #(.width(32)) bitselector_10 (.in(A), .out(bitselector_10_out), .sel({5{1'b1}}));
  xor xor_2 (xor_2_out, bitselector_5_out, bitselector_2_out);
  xnor xnor_3 (xnor_3_out, bitselector_7_out, bitselector_8_out);
  xnor xnor_4 (xnor_4_out, bitselector_9_out, bitselector_10_out);
  xor xor_3 (xor_3_out, bitselector_2_out, bitselector_6_out);
  Multiplexer #(.enable("false"), .select(4), .width(32)) multiplexer_1 (
    .in0(and_1_out), .in1(xor_1_out), .in2(shifter_1_out), .in3(shifter_2_out), .in4(shifter_3_out),
    .in5(adder_1_out), .in6(subtractor_1_out), .in7(shifter_4_out), .in8(and_2_out), .in9(subtractor_2_out),
    .in10(subtractor_3_out), .in11(adder_2_out), .in12(or_1_out), .in13(multiplier_1_out), .in14(and_3_out),
    .in15(not_2_out), .out(multiplexer_1_out), .sel(Codop));
  BitSelector #(.width(32)) bitselector_11 (.in(multiplier_1_cout), .out(bitselector_11_out), .sel({5{1'b0}}));
  and and_4 (and_4_out, xor_2_out, xnor_1_out);
  and and_5 (and_5_out, xnor_1_out, xor_3_out);
  and and_6 (and_6_out, xnor_3_out, xnor_2_out);
  and and_7 (and_7_out, xnor_2_out, xnor_4_out);
  BitSelector #(.width(32)) bitselector_12 (.in(B), .out(bitselector_12_out), .sel(subtractor_4_out));
  Subtractor #(.width(5)) subtractor_4 (.a(Shift), .b({5{1'b0}}), .out(subtractor_4_out));  // open: bin, bout
  Subtractor #(.width(5)) subtractor_5 (.a(5'b00001), .b(Shift), .out(subtractor_5_out));  // open: bin, bout
  BitSelector #(.width(32)) bitselector_13 (.in(B), .out(bitselector_13_out), .sel(subtractor_5_out));
  Multiplexer #(.enable("false"), .select(4)) multiplexer_2 (
    .in0(1'b0), .in1(1'b0), .in2(1'b0), .in3(1'b0), .in4(1'b0), .in5(and_4_out), .in6(and_6_out), .in7(1'b0),
    .in8(1'b0), .in9(1'b0), .in10(and_7_out), .in11(and_5_out), .in12(1'b0), .in13(1'b0), .in14(1'b0),
    .in15(1'b0), .out(Flags[0]), .sel(Codop));
  BitSelector #(.width(32)) bitselector_14 (.in(multiplexer_1_out), .out(Flags[3]), .sel({5{1'b1}}));
  Comparator #(.width(32)) comparator_1 (.a(multiplexer_1_out), .b({32{1'b0}}), .eq(Flags[2]));  // open: gt, lt
  Multiplexer #(.enable("false"), .select(4)) multiplexer_3 (
    .in0(1'b0), .in1(1'b0), .in2(bitselector_12_out), .in3(bitselector_13_out), .in4(bitselector_13_out),
    .in5(adder_1_cout), .in6(subtractor_1_bout), .in7(bitselector_13_out), .in8(1'b0), .in9(1'b0),
    .in10(subtractor_3_bout), .in11(adder_2_cout), .in12(1'b0), .in13(bitselector_11_out), .in14(1'b0),
    .in15(1'b0), .out(Flags[1]), .sel(Codop));
  Multiplexer #(.enable("false"), .select(4), .width(32)) multiplexer_4 (
    .in0(multiplexer_1_out), .in1(multiplexer_1_out), .in2(multiplexer_1_out), .in3(multiplexer_1_out),
    .in4(multiplexer_1_out), .in5(multiplexer_1_out), .in6(multiplexer_1_out), .in7(multiplexer_1_out),
    .in8(B), .in9(multiplexer_1_out), .in10(B), .in11(B), .in12(multiplexer_1_out), .in13(multiplexer_1_out),
    .in14(multiplexer_1_out), .in15(multiplexer_1_out), .out(S), .sel(Codop));

  // Notes on the sheet:
  //   Note: for ROR, C = N
  //   Note 2: assume that shift > 0 for LSL and LSR
  //   LSR
  //   ASR
  //   ADC
  //   SBC
  //   ROR
  //   TST
  //   RSB
  //   CMP
  //   CMN
  //   ORR
  //   MUL
  //   BIC
  //   MVN
  //   AND
  //   EOR
  //   LSL
endmodule
