// Logisim project BancDeRegistres.circ as structural Verilog: 1 circuit, main circuit BancRegistre
module BancRegistre (
  input  [31:0] DataIn,
  input  [2:0] RegA,
  input  [2:0] RegB,
  input  [2:0] RegDest,
  input  Clk,
  input  Reset,
  output [31:0] AOut,
  output [31:0] BOut,
  output [31:0] R0,
  output [31:0] R1,
  output [31:0] R2,
  output [31:0] R3,
  output [31:0] R4,
  output [31:0] R5,
  output [31:0] R6,
  output [31:0] R7
);

  wire [31:0] multiplexer_1_out;

  Multiplexer #(.enable("false"), .width(32)) multiplexer_1 (
    .in0(DataIn), .in1({32{1'b0}}), .out(multiplexer_1_out), .sel(Reset));
  Demultiplexer #(.enable("false"), .select(3), .width(32)) demultiplexer_1 (
    .out0(R0), .out1(R1), .out2(R2), .out3(R3), .out4(R4), .out5(R5), .out6(R6), .out7(R7),
    .in(multiplexer_1_out), .sel(RegDest));
  Multiplexer #(.enable("false"), .select(3), .width(32)) multiplexer_2 (
    .in0(R0), .in1(R1), .in2(R2), .in3(R3), .in4(R4), .in5(R5), .in6(R6), .in7(R7), .out(AOut), .sel(RegA));
  Multiplexer #(.enable("false"), .select(3), .width(32)) multiplexer_3 (
    .in0(R0), .in1(R1), .in2(R2), .in3(R3), .in4(R4), .in5(R5), .in6(R6), .in7(R7), .out(BOut), .sel(RegB));
endmodule
