// Logisim project Ctl_Conditional.circ as structural Verilog: 1 circuit, main circuit Conditional
module Conditional (
  input  Enable,
  input  [15:0] Instruction,
  input  Z,
  input  C,
  input  N,
  input  V,
  output [10:0] Offset,
  output Verified
);

  wire and_1_out, and_2_out, and_3_out, bitselector_1_out, multiplexer_2_out, not_1_out, not_2_out,
       not_3_out, not_4_out, or_1_out, or_2_out, or_3_out, xor_1_out;
  wire [10:0] bit_extender_1_out;

  BitSelector #(.width(16)) bitselector_1 (.in(Instruction), .out(bitselector_1_out), .sel(4'b1101));
  not not_1 (not_1_out, Z);
  not not_2 (not_2_out, C);
  not not_3 (not_3_out, N);
  not not_4 (not_4_out, V);
  assign bit_extender_1_out = {{3{Instruction[7]}}, Instruction[7:0]};  // Bit_Extender bit_extender_1
  Multiplexer #(.enable("false"), .width(11)) multiplexer_1 (
    .in0(bit_extender_1_out), .in1(Instruction[10:0]), .out(Offset), .sel(bitselector_1_out));
  and and_1 (and_1_out, N, V);
  xor xor_1 (xor_1_out, N, V);
  and and_2 (and_2_out, C, not_1_out);
  or or_1 (or_1_out, not_2_out, Z);
  and and_3 (and_3_out, not_1_out, and_1_out);
  or or_2 (or_2_out, Z, xor_1_out);
  or or_3 (or_3_out, bitselector_1_out, multiplexer_2_out);
  Multiplexer #(.enable("false"), .select(4)) multiplexer_2 (
    .in0(Z), .in1(not_1_out), .in2(C), .in3(not_2_out), .in4(N), .in5(not_3_out), .in6(V), .in7(not_4_out),
    .in8(and_2_out), .in9(or_1_out), .in10(and_1_out), .in11(xor_1_out), .in12(and_3_out), .in13(or_2_out),
    .in14(1'b1), .in15(1'b0), .out(multiplexer_2_out), .sel(Instruction[11:8]));
  and and_4 (Verified, Enable, or_3_out);
endmodule
