// Logisim project Ctl_Opcode_Decoder.circ as structural Verilog: 1 circuit, main circuit Opcode_Decoder
module Opcode_Decoder (
  input  [5:0] Opcode,
  output Shift,
  output Data_Processing,
  output Load_Store,
  output SP_Address,
  output Conditional
);

  and and_1 (Shift, ~Opcode[4], ~Opcode[5]);  // AND_Gate
  and and_2 (Data_Processing, ~Opcode[0], ~Opcode[1], ~Opcode[2], ~Opcode[3], Opcode[4], ~Opcode[5]);  // AND_Gate
  and and_3 (Load_Store, Opcode[2], ~Opcode[3], ~Opcode[4], Opcode[5]);  // AND_Gate
  and and_4 (SP_Address, Opcode[2], Opcode[3], ~Opcode[4], Opcode[5]);  // AND_Gate
  and and_5 (Conditional, Opcode[2], ~Opcode[3], Opcode[4], Opcode[5]);  // AND_Gate

  // Notes on the sheet:
  //   Shift, add, sub, mov
  //   Load/Store
  //   SP Address
  //   Conditional branch
  //   Data Processing
endmodule
