// Logisim project Ctl_Shift_Add_Sub_Mov.circ as structural Verilog: 1 circuit, main circuit Shift_Add_Sub_Mov
module Shift_Add_Sub_Mov (
  input  Enable,
  input  [15:0] Instruction,
  output [3:0] Flags_Update_Mask,
  output Carry,
  output Imm32_Enable,
  output [2:0] Rm,
  output [2:0] Rn,
  output [2:0] Rd,
  output [4:0] Imm5,
  output [31:0] Imm32,
  output [3:0] ALU_Opcode
);

  wire and_1_out, and_2_out, and_3_out, and_4_out, and_5_out, and_6_out, and_7_out, comparator_1_eq,
       multiplexer_3_out, multiplexer_7_out, or_1_out, or_3_out;
  wire [1:0] or_2_out;
  wire [2:0] multiplexer_2_out;
  wire [3:0] adder_1_out, multiplexer_4_out, multiplexer_5_out;
  wire [31:0] bit_extender_1_out, bit_extender_2_out, multiplexer_1_out, multiplexer_6_out, negator_1_out;

  or or_1 (or_1_out, Instruction[13], Instruction[11]);
  and and_1 (and_1_out, Instruction[13], Instruction[12]);
  and and_2 (and_2_out, ~Instruction[12], ~Instruction[11]);  // AND_Gate
  and and_3 (and_3_out, Instruction[13], Instruction[11]);
  and and_4 (and_4_out, Instruction[13], ~Instruction[12]);  // AND_Gate
  and and_5 (and_5_out, Instruction[12], or_1_out);
  and and_6 (and_6_out, ~Instruction[11], ~Instruction[12]);  // AND_Gate
  assign bit_extender_1_out = {{24{1'b0}}, Instruction[7:0]};  // Bit_Extender bit_extender_1
  Negator #(.width(32)) negator_1 (.in(bit_extender_1_out), .out(negator_1_out));
  assign bit_extender_2_out = {{29{1'b0}}, Instruction[8:6]};  // Bit_Extender bit_extender_2
  Multiplexer #(.enable("false"), .width(32)) multiplexer_1 (
    .in0(bit_extender_1_out), .in1(negator_1_out), .out(multiplexer_1_out), .sel(and_6_out));
  nand nand_1 (or_2_out[1], Instruction[13], and_2_out);
  or or_2 (or_2_out[0], and_3_out, and_5_out);
  and and_7 (and_7_out, Instruction[10], Instruction[11], Instruction[12]);
  Multiplexer #(.enable("false"), .width(3)) multiplexer_2 (
    .in0(Instruction[2:0]), .in1(Instruction[10:8]), .out(multiplexer_2_out), .sel(Instruction[13]));
  Multiplexer #(.enable("false")) multiplexer_3 (
    .in0(Instruction[9]), .in1(Instruction[11]), .out(multiplexer_3_out), .sel(Instruction[13]));
  Multiplexer #(.enable("false"), .width(4)) multiplexer_4 (
    .in0(4'b0010), .in1(4'b0101), .out(multiplexer_4_out), .sel(and_4_out));
  Multiplexer #(.enable("false"), .width(4)) multiplexer_5 (
    .in0(Instruction[14:11]), .in1(Instruction[15:12]), .out(multiplexer_5_out), .sel(and_1_out));
  Comparator #(.width(4)) comparator_1 (.a(4'b0110), .b(adder_1_out), .eq(comparator_1_eq));  // open: gt, lt
  or or_3 (or_3_out, and_7_out, Instruction[13]);
  Multiplexer #(.enable("false"), .width(32)) multiplexer_6 (
    .in0(bit_extender_2_out), .in1(multiplexer_1_out), .out(multiplexer_6_out), .sel(Instruction[13]));
  Multiplexer #(.enable("false")) multiplexer_7 (
    .in0(1'b0), .in1(multiplexer_3_out), .out(multiplexer_7_out), .sel(and_5_out));
  Adder #(.width(4)) adder_1 (
    .a(multiplexer_4_out), .b(multiplexer_5_out), .out(adder_1_out), .cin(multiplexer_7_out));  // open: cout
  Multiplexer #(.enable("false"), .width(4)) multiplexer_8 (
    .in0(4'b0000), .in1({2'b11, or_2_out}), .out(Flags_Update_Mask), .sel(Enable));
  and and_8 (Carry, Enable, comparator_1_eq);
  and and_9 (Imm32_Enable, Enable, or_3_out);
  Multiplexer #(.enable("false"), .width(3)) multiplexer_9 (
    .in0(3'b000), .in1(Instruction[8:6]), .out(Rm), .sel(Enable));
  Multiplexer #(.enable("false"), .width(3)) multiplexer_10 (
    .in0(3'b000), .in1(Instruction[5:3]), .out(Rn), .sel(Enable));
  Multiplexer #(.enable("false"), .width(3)) multiplexer_11 (
    .in0(3'b000), .in1(multiplexer_2_out), .out(Rd), .sel(Enable));
  Multiplexer #(.enable("false"), .width(5)) multiplexer_12 (
    .in0({5{1'b0}}), .in1(Instruction[10:6]), .out(Imm5), .sel(Enable));
  Multiplexer #(.enable("false"), .width(32)) multiplexer_13 (
    .in0({32{1'b0}}), .in1(multiplexer_6_out), .out(Imm32), .sel(Enable));
  Multiplexer #(.enable("false"), .width(4)) multiplexer_14 (
    .in0(4'b0000), .in1(adder_1_out), .out(ALU_Opcode), .sel(Enable));

  // Notes on the sheet:
  //   Note: ALU uses Rn register for shifts. Use Rn instead of Rm for shifts (immediate) here too
  //   Note 3: Imm32_Enable forces the use of the immediate for Rm register
  //   Note 2: MOV uses RSB ALU opcode with Imm8 reversed so that it is copied to output register
  //   Pull output low on Enable = 0
  //   only ADD and SUB use Rm
  //   Enable carry for SUB since it is reversed in ALU
  //   ALU will use Imm32 instead of Rm
endmodule
